# Fritzing sketch AgroLabIoT (saved by Fritzing 0.9.3b)
breadboards: 1

parts:
  WeMos_D1_Mini1 = WeMos D1 Mini  # not connected
  RHT1 = Humidity and Temperature Sensor RHT03
  U1 = BATTERY-2 [package=battery-aaa]
  Part1 = Soil Moisture Sensor
  U2 = BATTERY-2 [package=battery-aaa]

nets:
  VCC: RHT1.Vcc, U1.-1, Part1.VCC, U2.+1
  N1: RHT1.GND_2, U1.+1, Part1.GND, U2.-1
